# Fritzing sketch tanklevel1 (saved by Fritzing 0.9.0b)
breadboards: 1

parts:
  Part1 = Arduino Nano (Rev3.0)
  NRF24L1 = NRF24L01

nets:
  GND: Part1.GND, NRF24L1.GND
  N1: Part1.D9, NRF24L1.CE
  N2: Part1.D10, NRF24L1.CSN
  N3: Part1.D11/MOSI, NRF24L1.MOSI
  N4: Part1.D12/MISO, NRF24L1.MISO
  3V3: Part1.3V3, NRF24L1.VCC
  N5: Part1.D13/SCK, NRF24L1.SCK

custom parts:
  NRF24L01: NRF24L01 module
